# Fritzing sketch reloj (saved by Fritzing 0.9.4)

parts:
  S1 = Pushbutton [package="[THT]"]
  R1 = Resistor [tolerance=±5% resistance=1k package="2010 [SMD]"]
  Mod1 = Heltec WiFi Kit 32 [part_number=HTIT-WB32LA]
  BAT1 = LIPO-1000mAh [package=lipo-1000]  # not connected

nets:
  N1: S1.Pin_1, S1.Pin_2, Mod1.pin_17
  N2: S1.Pin_3, S1.Pin_4, R1.Pin_0, Mod1.pin_12

custom parts:
  Heltec WiFi Kit 32: Heltec WiFi Kit 32 WiFi Kit 32 is a classic IoT dev-board designed & produced by Heltec Automation(TM). It’s a highly integrated product based on ESP32 + SX127x, it has Wi-Fi, BLE, LoRa functions, also Li-Po battery management system, 0.96″ OLED are also included. It’s the best choice for smart cities, smart farms, smart home, and IoT makers.
